# Fritzing sketch circuito-cybertruck (saved by Fritzing 1.0.4)
breadboards: 1

parts:
  ESP32_DEVKIT_V1 = DOIT Esp32 DevKit v1 (30 pins long, 11 pins width) [part_number=ESP32S-PIN30]
  LM2596_(_STEP-DOWN)_6V = RioRand LM2596
  MOTORREDUCTOR_48_1 = gear-motor
  SERVOMOTOR = Basic Servo
  SWITCH = SPST Switch [package=r_sw_th]
  L293D = L293D [package=THT]
  LED = LED - 5mm [color="Red (633nm)" current=0.030A package="5 mm [THT]"]
  REGULADOR_DE_VOLTAJE_5V_(L7805) = Voltage Regulator [package=to220-igo]
  BATERIAS_PRINCIPALES = Battery [internal_resistance=0.1Ω]
  VCC1 = Battery [internal_resistance=0.1Ω]  # not connected
  R2 = Resistor [tolerance=±5% resistance=220 package="0603 [SMD]"]

nets:
  N1: ESP32_DEVKIT_V1.D25, L293D.In_1
  N2: ESP32_DEVKIT_V1.D26, L293D.In_2
  N3: ESP32_DEVKIT_V1.D27, L293D.Enable_1
  N4: ESP32_DEVKIT_V1.D12, SERVOMOTOR.pulse
  N5: ESP32_DEVKIT_V1.D13, R2.Pin_0
  VIN: ESP32_DEVKIT_V1.VIN, SERVOMOTOR.vcc, L293D.+V, REGULADOR_DE_VOLTAJE_5V_(L7805).OUT
  N6: LM2596_(_STEP-DOWN)_6V.Pin_1, SWITCH.O, SWITCH.P, BATERIAS_PRINCIPALES.+
  N7: LM2596_(_STEP-DOWN)_6V.Pin_2, LM2596_(_STEP-DOWN)_6V.Pin_4, SERVOMOTOR.gnd, L293D.0V, LED.cathode, REGULADOR_DE_VOLTAJE_5V_(L7805).IN, BATERIAS_PRINCIPALES.-
  N8: LM2596_(_STEP-DOWN)_6V.Pin_3, L293D.+Vmotor
  N9: MOTORREDUCTOR_48_1.pin_2, L293D.Out_1_(_Controlled_by_Enable_1_)

notes:
  voltaje cable rojo 11.1V
  Pin A01 y A02 motor A
  Cable naranja:[Alimentacion para Esp32 y el integrado L293d
  ALIMENTACION :
  Cable rojo : 11 voltios.
  Cable rosa : 6 voltios.
  Cable naranja : 5 voltios.
  Cable negro : Tierra comun.
  Driver Motores (puente H)

custom parts:
  DOIT Esp32 DevKit v1 (30 pins long, 11 pins width): The DOIT Esp32 DevKit v1 is one of the development board created by DOIT to evaluate the ESP-WROOM-32 module. It is based on the ESP32 microcontroller that boasts Wifi, Bluetooth, Ethernet and Low Power support all in a single chip. (vanepp) made breadboard work, adjusted pin numbering and labels and reduced size of schematic and cleaned up pcb. This chip is 30pins long (2 x15) and 11 pins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
